# Fritzing sketch ms-led-dimmer-rgbw (saved by Fritzing 0.9.3b)
circuit board: 4cm x 2cm
breadboards: 1

parts:
  J1 = Screw terminal - 2 pins [part_number=input package=THT]
  R4 = Resistor [tolerance=±5% resistance=10k package=THT]
  J2 = Screw terminal - 2 pins [part_number=output package=THT]
  Q1 = Basic FET N-Channel [package="TO220 [THT]"]
  C1 = Electrolytic Capacitor [capacitance=100nF package="100 mil [THT, electrolytic]"]
  R1 = Resistor [tolerance=±5% resistance=470 package=THT]
  R3 = Resistor [tolerance=±5% resistance=100 package=THT]
  LED1 = LED - 3mm [color="Red (633nm)" package="3 mm [THT]"]
  U1 = Optocoupler [package=THT]
  R2 = Resistor [tolerance=±5% resistance=1k package=THT]
  JP1 = Header 3 [package=molex-1x3_lock]

nets:
  12V: J1.pin1, J2.pin1, U1.Pin_5
  GND: J1.pin2, R4.Pin_0, Q1.source, C1.-, LED1.cathode, U1.Pin_2, JP1.1
  N1: R4.Pin_1, Q1.gate, R3.Pin_1
  N2: J2.pin2, Q1.drain
  N3: C1.+, R1.Pin_1, U1.Pin_1
  N4: R1.Pin_0, JP1.2
  N5: R3.Pin_0, U1.Pin_4, R2.Pin_0
  N6: LED1.anode, R2.Pin_1
